// Digital circuit CPU.dig as structural Verilog
module CPU (
  input  [63:0] Databus_Manual_Input,
  input  CPU_Clock
);

  wire clock, Databus_Manual_Switch_out, Manual_Clock_Stepper_out, Manual_Stepping_out;
  wire [63:0] databus;

  DipSwitch #(.dipDefault("true")) Manual_Stepping (.out(Manual_Stepping_out));
  Button Manual_Clock_Stepper (.out(Manual_Clock_Stepper_out));
  assign clock = Manual_Stepping_out ? Manual_Clock_Stepper_out : 1'bz;  // Driver driver_1
  assign clock = ~Manual_Stepping_out ? CPU_Clock : 1'bz;  // DriverInvSel driverinvsel_1
  assign databus = Databus_Manual_Switch_out ? Databus_Manual_Input : 64'bz;  // Driver driver_2
  DipSwitch Databus_Manual_Switch (.out(Databus_Manual_Switch_out));

  // Notes on the sheet:
  //   Clock Control
  //   Manual Databus Control
endmodule
